// Logisim project Pedra-Pape-Tesoura.circ as structural Verilog: 1 circuit, main circuit main
module main (
  input  in_1,
  input  in_2,
  input  Tesoura,
  input  Papel,
  input  Pedra,
  input  Pedraa,
  input  Papell,
  input  Tesouraa
);

  wire and_1_out, and_2_out, and_3_out, and_4_out, and_5_out, and_6_out, nor_1_out, nor_2_out, or_1_out,
       or_2_out;

  nor nor_1 (nor_1_out, in_1, Pedra, Papel, Tesoura);
  LED led_1 (.in(nor_1_out));
  and and_1 (and_1_out, Tesoura, Papell);
  and and_2 (and_2_out, Papel, Pedraa);
  or or_1 (or_1_out, and_1_out, and_2_out, and_3_out);
  LED led_2 (.in(or_1_out));
  and and_3 (and_3_out, Pedra, Tesouraa);
  and and_4 (and_4_out, Tesoura, Pedraa);
  and and_5 (and_5_out, Pedra, Papell);
  or or_2 (or_2_out, and_4_out, and_5_out, and_6_out);
  LED led_3 (.in(or_2_out));
  and and_6 (and_6_out, Papel, Tesouraa);
  nor nor_2 (nor_2_out, Tesouraa, Papell, Pedraa, in_2);
  LED led_4 (.in(nor_2_out));

  // Notes on the sheet:
  //   Sem Vencedores
  //   Jogador 1
  //   Jogador 1 Vencedor
  //   Jogador 2
  //   Jogador 2 Vencedor
  //   Sem Vencedores
endmodule
