// Logisim project Solucao_Pedra_Papel_Tesoura.circ as structural Verilog: 3 circuits, main circuit main
module main (
  input  Pedra_1,
  input  Papel_1,
  input  Tesoura_1,
  input  Pedra_2,
  input  Papel_2,
  input  Tesoura_2,
  output Jogador_1_ganhou,
  output empate,
  output Jogador_2_ganhou
);

  wire codificador_1_c0, codificador_1_c1, codificador_2_c0, codificador_2_c1;

  Codificador codificador_1 (.A(Pedra_1), .B(Papel_1), .C(Tesoura_1), .c1(codificador_1_c1), .c0(codificador_1_c0));
  Codificador codificador_2 (.A(Pedra_2), .B(Papel_2), .C(Tesoura_2), .c1(codificador_2_c1), .c0(codificador_2_c0));
  controleJogo controlejogo_1 (
    .C1P1(codificador_1_c1), .C0P1(codificador_1_c0), .C1P2(codificador_2_c1), .C0P2(codificador_2_c0),
    .win_p1(Jogador_1_ganhou), .die(empate), .win_p2(Jogador_2_ganhou));
  LED led_1 (.in(Jogador_1_ganhou));
  LED led_2 (.in(empate));
  LED led_3 (.in(Jogador_2_ganhou));

  // Notes on the sheet:
  //   Jogador_1
  //   Jogador_2
  //   c1 c0
  //   0 0 -> Invalido
  //   0 1 -> pedra
  //   1 0 -> papel
  //   1 1 -> tesoura
endmodule

module Codificador (
  input  A,
  input  B,
  input  C,
  output c1,
  output c0
);

  wire and_1_out, and_2_out, and_3_out, and_4_out, not_1_out, not_2_out, not_3_out;

  not not_1 (not_1_out, A);
  not not_2 (not_2_out, B);
  not not_3 (not_3_out, C);
  and and_1 (and_1_out, not_1_out, not_2_out, C);
  and and_2 (and_2_out, not_1_out, B, not_3_out);
  and and_3 (and_3_out, not_1_out, not_2_out, C);
  and and_4 (and_4_out, A, not_2_out, not_3_out);
  or or_1 (c1, and_1_out, and_2_out);
  or or_2 (c0, and_3_out, and_4_out);
endmodule

module controleJogo (
  input  C1P1,
  input  C0P1,
  input  C1P2,
  input  C0P2,
  output win_p1,
  output die,
  output win_p2
);

  wire and_1_out, and_2_out, and_3_out, and_4_out, and_5_out, and_6_out, and_7_out, and_8_out, and_9_out,
       not_1_out, not_2_out, not_3_out, not_4_out;

  not not_1 (not_1_out, C1P1);
  not not_2 (not_2_out, C0P1);
  not not_3 (not_3_out, C1P2);
  not not_4 (not_4_out, C0P2);
  and and_1 (and_1_out, not_1_out, C0P1, C1P2, C0P2);
  and and_2 (and_2_out, C1P1, not_2_out, not_3_out, C0P2);
  and and_3 (and_3_out, C1P1, C0P1, C1P2, not_4_out);
  and and_4 (and_4_out, not_1_out, C0P1, not_3_out, C0P2);
  and and_5 (and_5_out, C1P1, not_2_out, C1P2, not_4_out);
  and and_6 (and_6_out, C1P1, C0P1, C1P2, C0P2);
  and and_7 (and_7_out, not_1_out, C0P1, C1P2, not_4_out);
  and and_8 (and_8_out, C1P1, not_2_out, C1P2, C0P2);
  and and_9 (and_9_out, C1P1, C0P1, not_3_out, C0P2);
  or or_1 (win_p1, and_1_out, and_2_out, and_3_out);
  or or_2 (die, and_4_out, and_5_out, and_6_out);
  or or_3 (win_p2, and_7_out, and_8_out, and_9_out);
endmodule
