// Logisim project Decodificador_Gray_To_Excesso_3.circ as structural Verilog: 1 circuit, main circuit main
module main (
  input  A,
  input  B,
  input  C,
  input  D,
  output s1,
  output s2,
  output s3,
  output s4
);

  wire and_1_out, and_2_out, and_3_out, and_4_out, and_5_out, and_6_out, and_7_out, and_8_out, and_9_out,
       and_10_out, not_1_out, not_2_out, not_3_out;

  not not_1 (not_1_out, A);
  not not_2 (not_2_out, B);
  not not_3 (not_3_out, C);
  not not_4 (s3, D);
  and and_1 (and_1_out, B, not_3_out);
  and and_2 (and_2_out, B, D);
  and and_3 (and_3_out, not_2_out, D);
  and and_4 (and_4_out, C, s3);
  and and_5 (and_5_out, A, D);
  and and_6 (and_6_out, not_2_out, not_3_out, s3);
  and and_7 (and_7_out, not_2_out, C, D);
  and and_8 (and_8_out, not_1_out, B, not_3_out, D);
  and and_9 (and_9_out, B, C, s3);
  and and_10 (and_10_out, A, s3);
  or or_1 (s1, and_1_out, and_2_out);
  or or_2 (s2, and_3_out, and_4_out, and_5_out);
  or or_3 (s4, and_6_out, and_7_out, and_8_out, and_9_out, and_10_out);
endmodule
