// Logisim project project.circ as structural Verilog: 3 circuits, main circuit main
module main (
  input  [3:0] A,
  input  [3:0] B,
  output [7:0] out_3
);

  wire and_1_out, and_2_out, and_3_out, and_4_out, and_5_out, and_6_out, and_7_out, and_8_out, and_9_out,
       and_10_out, and_11_out, and_12_out, and_13_out, and_14_out, and_15_out, ms_1_c, ms_1_s, ms_2_c,
       ms_3_c, ms_4_c, sc_2_cout, sc_2_s, sc_3_cout, sc_4_cout, sc_4_s, sc_5_cout, sc_5_s, sc_6_cout,
       sc_7_cout, sc_7_s, sc_8_cout, sc_8_s;

  and and_1 (and_1_out, A[3], B[3]);
  SC sc_1 (.S(out_3[6]), .Cout(out_3[7]), .C(sc_3_cout), .B0(sc_2_cout), .A0(and_1_out));
  and and_2 (and_2_out, A[3], B[2]);
  SC sc_2 (.S(sc_2_s), .Cout(sc_2_cout), .C(sc_4_cout), .B0(ms_1_c), .A0(and_2_out));
  MS ms_1 (.C(ms_1_c), .S(ms_1_s), .A0(sc_5_cout), .B0(and_4_out));
  and and_3 (and_3_out, A[2], B[3]);
  SC sc_3 (.S(out_3[5]), .Cout(sc_3_cout), .C(sc_6_cout), .B0(sc_2_s), .A0(and_3_out));
  and and_4 (and_4_out, A[3], B[1]);
  and and_5 (and_5_out, A[2], B[2]);
  SC sc_4 (.S(sc_4_s), .Cout(sc_4_cout), .C(sc_7_cout), .B0(ms_1_s), .A0(and_5_out));
  and and_6 (and_6_out, A[3], B[0]);
  and and_7 (and_7_out, B[1], A[2]);
  SC sc_5 (.S(sc_5_s), .Cout(sc_5_cout), .C(sc_8_cout), .B0(and_6_out), .A0(and_7_out));
  and and_8 (and_8_out, B[3], A[1]);
  SC sc_6 (.S(out_3[4]), .Cout(sc_6_cout), .C(ms_2_c), .B0(sc_4_s), .A0(and_8_out));
  and and_9 (and_9_out, B[2], A[1]);
  SC sc_7 (.S(sc_7_s), .Cout(sc_7_cout), .C(ms_3_c), .B0(sc_5_s), .A0(and_9_out));
  and and_10 (and_10_out, A[2], B[0]);
  and and_11 (and_11_out, B[3], A[0]);
  MS ms_2 (.C(ms_2_c), .S(out_3[3]), .A0(and_11_out), .B0(sc_7_s));
  and and_12 (and_12_out, B[1], A[1]);
  SC sc_8 (.S(sc_8_s), .Cout(sc_8_cout), .C(ms_4_c), .B0(and_10_out), .A0(and_12_out));
  MS ms_3 (.C(ms_3_c), .S(out_3[2]), .A0(and_14_out), .B0(sc_8_s));
  and and_13 (and_13_out, A[1], B[0]);
  MS ms_4 (.C(ms_4_c), .S(out_3[1]), .A0(and_15_out), .B0(and_13_out));
  and and_14 (and_14_out, B[2], A[0]);
  and and_15 (and_15_out, B[1], A[0]);
  and and_16 (out_3[0], A[0], B[0]);
endmodule

module MS (
  input  A0,
  input  B0,
  output C,
  output S
);

  and and_1 (C, A0, B0);
  xor xor_1 (S, A0, B0);
endmodule

module SC (
  input  C,
  input  B0,
  input  A0,
  output Cout,
  output S
);

  wire and_1_out, and_2_out, xor_1_out;

  and and_1 (and_1_out, B0, A0);
  xor xor_1 (xor_1_out, B0, A0);
  and and_2 (and_2_out, xor_1_out, C);
  xor xor_2 (S, C, xor_1_out);
  or or_1 (Cout, and_1_out, and_2_out);
endmodule
