// Logisim project BancodeRegistradores.circ as structural Verilog: 15 circuits, main circuit Main
module Main (
  input  [7:0] in_1,
  input  SelValor,
  input  [1:0] in_3,
  input  [1:0] in_4,
  input  [1:0] in_5,
  input  Escreve,
  input  [2:0] in_7,
  output [7:0] out_8,
  output [7:0] out_9,
  output out_10,
  output out_11,
  output [7:0] out_12
);

  wire [7:0] multiplexer_1_out;

  Multiplexer #(.enable("false"), .width(8)) multiplexer_1 (
    .in0(out_12), .in1(in_1), .out(multiplexer_1_out), .sel(SelValor));
  BancoRegistradores bancoregistradores_1 (
    .VA(out_9), .VB(out_8), .Escreve(Escreve), .VW(multiplexer_1_out), .RW(in_3), .RA(in_4), .RB(in_5));
  Selecao selecao_1 (.Overflow(out_11), .out_5(out_10), .out_6(out_12), .in_1(out_9), .in_2(out_8), .Operacao(in_7));

  // Notes on the sheet:
  //   76543210
  //   00 - Primeiro Registrador
  //   01 - Segundo Registrador
  //   10 - Terceiro Registrador
  //   11 - Quarto Registrador
  //   000 - A * B
  //   001 - ~B
  //   010 - A XOR B
  //   011 - A + B
  //   100 - A OR B
  //   101 - A / B
  //   110 - A - B
  //   111 - A AND B
endmodule

module Registradores (
  input  [7:0] Entrada,
  input  in_2,
  output [7:0] Saida
);

  D_Flip_Flop d_ff_1 (.clk(in_2), .D(Entrada[7]), .Q(Saida[7]));  // open: Qn, preset, reset
  D_Flip_Flop d_ff_2 (.clk(in_2), .D(Entrada[6]), .Q(Saida[6]));  // open: Qn, preset, reset
  D_Flip_Flop d_ff_3 (.clk(in_2), .D(Entrada[5]), .Q(Saida[5]));  // open: Qn, preset, reset
  D_Flip_Flop d_ff_4 (.clk(in_2), .D(Entrada[4]), .Q(Saida[4]));  // open: Qn, preset, reset
  D_Flip_Flop d_ff_5 (.clk(in_2), .D(Entrada[3]), .Q(Saida[3]));  // open: Qn, preset, reset
  D_Flip_Flop d_ff_6 (.clk(in_2), .D(Entrada[2]), .Q(Saida[2]));  // open: Qn, preset, reset
  D_Flip_Flop d_ff_7 (.clk(in_2), .D(Entrada[1]), .Q(Saida[1]));  // open: Qn, preset, reset
  D_Flip_Flop d_ff_8 (.clk(in_2), .D(Entrada[0]), .Q(Saida[0]));  // open: Qn, preset, reset
endmodule

module BancoRegistradores (
  input  [7:0] VW,
  input  [1:0] RA,
  input  Escreve,
  input  [1:0] RB,
  input  [1:0] RW,
  output [7:0] VA,
  output [7:0] VB
);

  wire demultiplexer_1_out0, demultiplexer_1_out1, demultiplexer_1_out2, demultiplexer_1_out3;
  wire [7:0] registradores_1_saida, registradores_2_saida, registradores_3_saida, registradores_4_saida;

  Demultiplexer #(.enable("false"), .select(2)) demultiplexer_1 (
    .out0(demultiplexer_1_out0), .out1(demultiplexer_1_out1), .out2(demultiplexer_1_out2),
    .out3(demultiplexer_1_out3), .in(Escreve), .sel(RW));
  Registradores registradores_1 (.Saida(registradores_1_saida), .Entrada(VW), .in_2(demultiplexer_1_out0));
  Registradores registradores_2 (.Saida(registradores_2_saida), .Entrada(VW), .in_2(demultiplexer_1_out1));
  Registradores registradores_3 (.Saida(registradores_3_saida), .Entrada(VW), .in_2(demultiplexer_1_out2));
  Registradores registradores_4 (.Saida(registradores_4_saida), .Entrada(VW), .in_2(demultiplexer_1_out3));
  Multiplexer #(.enable("false"), .select(2), .width(8)) multiplexer_1 (
    .in0(registradores_1_saida), .in1(registradores_2_saida), .in2(registradores_3_saida),
    .in3(registradores_4_saida), .out(VA), .sel(RA));
  Multiplexer #(.enable("false"), .select(2), .width(8)) multiplexer_2 (
    .in0(registradores_1_saida), .in1(registradores_2_saida), .in2(registradores_3_saida),
    .in3(registradores_4_saida), .out(VB), .sel(RB));
endmodule

module B (
  input  [7:0] in_1,
  output [7:0] out_2
);

  not not_1 (out_2[0], in_1[7]);
  not not_2 (out_2[1], in_1[6]);
  not not_3 (out_2[2], in_1[5]);
  not not_4 (out_2[3], in_1[4]);
  not not_5 (out_2[4], in_1[3]);
  not not_6 (out_2[5], in_1[2]);
  not not_7 (out_2[6], in_1[1]);
  not not_8 (out_2[7], in_1[0]);
endmodule

module Soma8Bits (
  input  [7:0] in_1,
  input  [7:0] in_2,
  output Overflow,
  output [7:0] out_4
);

  wire ms_1_c, sc_2_cout, sc_3_cout, sc_4_cout, sc_5_cout, sc_6_cout, sc_7_cout;

  SC sc_1 (.S(out_4[7]), .Cout(Overflow), .C(sc_2_cout), .B(in_1[7]), .A(in_2[7]));
  SC sc_2 (.S(out_4[6]), .Cout(sc_2_cout), .C(sc_3_cout), .B(in_1[6]), .A(in_2[6]));
  SC sc_3 (.S(out_4[5]), .Cout(sc_3_cout), .C(sc_4_cout), .B(in_1[5]), .A(in_2[5]));
  SC sc_4 (.S(out_4[4]), .Cout(sc_4_cout), .C(sc_5_cout), .B(in_1[4]), .A(in_2[4]));
  SC sc_5 (.S(out_4[3]), .Cout(sc_5_cout), .C(sc_6_cout), .B(in_1[3]), .A(in_2[3]));
  SC sc_6 (.S(out_4[2]), .Cout(sc_6_cout), .C(sc_7_cout), .B(in_1[2]), .A(in_2[2]));
  SC sc_7 (.S(out_4[1]), .Cout(sc_7_cout), .C(ms_1_c), .B(in_1[1]), .A(in_2[1]));
  MS ms_1 (.C(ms_1_c), .S(out_4[0]), .A(in_1[0]), .B(in_2[0]));

  // Notes on the sheet:
  //   B
  //   A
endmodule

module Subtracao8Bits (
  input  [7:0] in_1,
  input  [7:0] in_2,
  output Overflow,
  output [7:0] out_4
);

  wire subtracao_2_borrowout, subtracao_3_borrowout, subtracao_4_borrowout, subtracao_5_borrowout,
       subtracao_6_borrowout, subtracao_7_borrowout, subtracao_8_borrowout;

  Subtracao subtracao_1 (
    .Borrowout(Overflow), .S(out_4[7]), .Borrowin(subtracao_2_borrowout), .A(in_2[7]), .B(in_1[7]));
  Subtracao subtracao_2 (
    .Borrowout(subtracao_2_borrowout), .S(out_4[6]), .Borrowin(subtracao_3_borrowout), .A(in_2[6]),
    .B(in_1[6]));
  Subtracao subtracao_3 (
    .Borrowout(subtracao_3_borrowout), .S(out_4[5]), .Borrowin(subtracao_4_borrowout), .A(in_2[5]),
    .B(in_1[5]));
  Subtracao subtracao_4 (
    .Borrowout(subtracao_4_borrowout), .S(out_4[4]), .Borrowin(subtracao_5_borrowout), .A(in_2[4]),
    .B(in_1[4]));
  Subtracao subtracao_5 (
    .Borrowout(subtracao_5_borrowout), .S(out_4[3]), .Borrowin(subtracao_6_borrowout), .A(in_2[3]),
    .B(in_1[3]));
  Subtracao subtracao_6 (
    .Borrowout(subtracao_6_borrowout), .S(out_4[2]), .Borrowin(subtracao_7_borrowout), .A(in_2[2]),
    .B(in_1[2]));
  Subtracao subtracao_7 (
    .Borrowout(subtracao_7_borrowout), .S(out_4[1]), .Borrowin(subtracao_8_borrowout), .A(in_2[1]),
    .B(in_1[1]));
  Subtracao subtracao_8 (.Borrowout(subtracao_8_borrowout), .S(out_4[0]), .Borrowin(1'b0), .A(in_2[0]), .B(in_1[0]));

  // Notes on the sheet:
  //   B
  //   A
endmodule

module MS (
  input  A,
  input  B,
  output C,
  output S
);

  and and_1 (C, A, B);
  xor xor_1 (S, A, B);
endmodule

module SC (
  input  C,
  input  B,
  input  A,
  output Cout,
  output S
);

  wire and_1_out, and_2_out, xor_1_out;

  and and_1 (and_1_out, B, A);
  xor xor_1 (xor_1_out, B, A);
  and and_2 (and_2_out, xor_1_out, C);
  xor xor_2 (S, C, xor_1_out);
  or or_1 (Cout, and_1_out, and_2_out);
endmodule

module Divisor (
  input  [7:0] A,
  input  [7:0] B,
  output [7:0] out_3
);

  Divider divider_1 (.a(A), .b(B), .out(out_3));  // open: upper, rem
endmodule

module Multiplicador (
  input  [7:0] A,
  input  [7:0] B,
  output [7:0] out_3
);

  Multiplier multiplier_1 (.a(A), .b(B), .out(out_3));  // open: cin, cout
endmodule

module Subtracao (
  input  B,
  input  A,
  input  Borrowin,
  output S,
  output Borrowout
);

  wire and_1_out, and_2_out, and_3_out, and_4_out, and_5_out, and_6_out, and_7_out, not_1_out, not_2_out,
       not_3_out, not_4_out, not_5_out, not_6_out, not_7_out, not_8_out;

  not not_1 (not_1_out, A);
  not not_2 (not_2_out, B);
  not not_3 (not_3_out, A);
  not not_4 (not_4_out, Borrowin);
  not not_5 (not_5_out, B);
  not not_6 (not_6_out, Borrowin);
  not not_7 (not_7_out, A);
  not not_8 (not_8_out, A);
  and and_1 (and_1_out, not_1_out, not_2_out, Borrowin);
  and and_2 (and_2_out, not_3_out, B, not_4_out);
  and and_3 (and_3_out, A, not_5_out, not_6_out);
  and and_4 (and_4_out, A, B, Borrowin);
  and and_5 (and_5_out, not_7_out, Borrowin);
  and and_6 (and_6_out, not_8_out, B);
  and and_7 (and_7_out, B, Borrowin);
  or or_1 (S, and_1_out, and_2_out, and_3_out, and_4_out);
  or or_2 (Borrowout, and_5_out, and_6_out, and_7_out);
endmodule

module AXORB (
  input  [7:0] B,
  input  [7:0] in_2,
  output [7:0] out_3
);

  xor xor_1 (out_3[7], B[7], in_2[7]);
  xor xor_2 (out_3[6], B[6], in_2[6]);
  xor xor_3 (out_3[5], B[5], in_2[5]);
  xor xor_4 (out_3[4], B[4], in_2[4]);
  xor xor_5 (out_3[3], B[3], in_2[3]);
  xor xor_6 (out_3[2], B[2], in_2[2]);
  xor xor_7 (out_3[1], B[1], in_2[1]);
  xor xor_8 (out_3[0], B[0], in_2[0]);

  // Notes on the sheet:
  //   A
endmodule

module ANORB (
  input  [7:0] in_1,
  input  [7:0] in_2,
  output [7:0] out_3
);

  nor nor_1 (out_3[7], in_1[7], in_2[7]);
  nor nor_2 (out_3[6], in_1[6], in_2[6]);
  nor nor_3 (out_3[5], in_1[5], in_2[5]);
  nor nor_4 (out_3[4], in_1[4], in_2[4]);
  nor nor_5 (out_3[3], in_1[3], in_2[3]);
  nor nor_6 (out_3[2], in_1[2], in_2[2]);
  nor nor_7 (out_3[1], in_1[1], in_2[1]);
  nor nor_8 (out_3[0], in_1[0], in_2[0]);

  // Notes on the sheet:
  //   A
  //   B
endmodule

module ANANDB (
  input  [7:0] in_1,
  input  [7:0] in_2,
  output [7:0] out_3
);

  nand nand_1 (out_3[7], in_1[7], in_2[7]);
  nand nand_2 (out_3[6], in_1[6], in_2[6]);
  nand nand_3 (out_3[5], in_1[5], in_2[5]);
  nand nand_4 (out_3[4], in_1[4], in_2[4]);
  nand nand_5 (out_3[3], in_1[3], in_2[3]);
  nand nand_6 (out_3[2], in_1[2], in_2[2]);
  nand nand_7 (out_3[1], in_1[1], in_2[1]);
  nand nand_8 (out_3[0], in_1[0], in_2[0]);

  // Notes on the sheet:
  //   A
  //   B
endmodule

module Selecao (
  input  [7:0] in_1,
  input  [7:0] in_2,
  input  [2:0] Operacao,
  output Overflow,
  output out_5,
  output [7:0] out_6
);

  wire [7:0] anandb_1_out_3, anorb_1_out_3, axorb_1_out_3, b_1_out_2, divisor_1_out_3, multiplicador_1_out_3,
       soma8bits_1_out_4, subtracao8bits_1_out_4;

  Multiplicador multiplicador_1 (.out_3(multiplicador_1_out_3), .B(in_2), .A(in_1));
  B b_1 (.out_2(b_1_out_2), .in_1(in_2));
  AXORB axorb_1 (.out_3(axorb_1_out_3), .in_2(in_1), .B(in_2));
  Soma8Bits soma8bits_1 (.Overflow(Overflow), .out_4(soma8bits_1_out_4), .in_2(in_2), .in_1(in_1));
  ANORB anorb_1 (.out_3(anorb_1_out_3), .in_2(in_1), .in_1(in_2));
  Divisor divisor_1 (.out_3(divisor_1_out_3), .B(in_2), .A(in_1));
  Subtracao8Bits subtracao8bits_1 (.Overflow(out_5), .out_4(subtracao8bits_1_out_4), .in_1(in_2), .in_2(in_1));
  ANANDB anandb_1 (.out_3(anandb_1_out_3), .in_2(in_1), .in_1(in_2));
  Multiplexer #(.enable("false"), .select(3), .width(8)) multiplexer_1 (
    .in0(multiplicador_1_out_3), .in1(b_1_out_2), .in2(axorb_1_out_3), .in3(soma8bits_1_out_4),
    .in4(anorb_1_out_3), .in5(divisor_1_out_3), .in6(subtracao8bits_1_out_4), .in7(anandb_1_out_3),
    .out(out_6), .sel(Operacao));
  ANANDB anandb_2 ();  // open: out_3, in_2, in_1

  // Notes on the sheet:
  //   A
  //   B
  //   A
  //   B
  //   000 - A * B
  //   001 - ~B
  //   010 - A XOR B
  //   011 - A + B
  //   100 - A NOR B
  //   101 - A / B
  //   110 - A - B
  //   111 - A AND B
endmodule
